# Fritzing sketch SML_power (saved by Fritzing 0.9.10b)

parts:
  M1 = DOIT Esp32 DevKit v1 (30 pins long, 11 pins width) [part_number=ESP32S-PIN30]
  NEOPIXEL1 = Neopixel Strip -- White (30/m) [part_number=1376]  # not connected
  Componente1 = Lithium Ion Polymer Battery 3.7v 1200mAh [part_number=258]
  M2 = TP4056 Module [part_number=HW-107]
  NEOPIXEL2 = White Light Strip
  HLK-PM3 = HLK-PM01
  JP1 = Header 6 [package=1x06-smd]
  MT3608 = mini boost module
  Q1 = Basic FET P-Channel [package="D2Pak [SMD]"]
  D1 = Schottky Diode [part_number=1N5817 package="300 mil [THT]"]
  R1 = Resistor [tolerance=±5% power=0.25 resistance=10k package=THT]
  HLK-PM2 = HLK-PM01
  J1 = Generic male header - 4 pins [form="♂ (male)" package=THT]
  DHT1 = DHT22 Humidity and Temperature Sensor  # not connected

nets:
  3V3: M1.3V3, J1.VCC
  GND: M1.GND, MT3608.Pin_3, J1.GND
  N1: M1.VIN, MT3608.Pin_4
  N2: Componente1.positive, M2.BAT+
  N3: Componente1.negative, M2.BAT-
  N4: M2.GND, HLK-PM2.-Vo
  N5: M2.OUT-#1, MT3608.Pin_1, R1.Pin_1
  N6: M2.OUT-#4, Q1.drain
  N7: M2.VCC, Q1.Gate, D1.anode, R1.Pin_0, HLK-PM2.+Vo
  N8: NEOPIXEL2.+5V, J1.NC#7
  N9: NEOPIXEL2.GND, HLK-PM3.-Vo
  N10: HLK-PM3.AC#0, HLK-PM2.AC#0
  N11: HLK-PM3.AC#1, HLK-PM2.AC#1
  N12: HLK-PM3.+Vo, J1.C#8
  N13: JP1.6, J1.NC#4
  N14: MT3608.Pin_2, Q1.source, D1.cathode

notes:
  110 V AC.
  Tira de 24 neopixels
  Leds blancos alta potencia de la lampara
  Fuente original de la lampara
  Load sharing circuito MOSFET P (GDS)
  DC-DC boost Converter
  Modulo Bluetooth con amplificador
  Esp 32
  Sensor temperatura y humedad DHT22
  Fuente 5v de salida
  Modulo de carga TP4056
  Bateria LiPO
  Modulo rele

custom parts:
  DOIT Esp32 DevKit v1 (30 pins long, 11 pins width): The DOIT Esp32 DevKit v1 is one of the development board created by DOIT to evaluate the ESP-WROOM-32 module. It is based on the ESP32 microcontroller that boasts Wifi, Bluetooth, Ethernet and Low Power support all in a single chip. (vanepp) made breadboard work, adjusted pin numbering and labels and reduced size of schematic and cleaned up pcb. This chip is 30pins long (2 x15) and 11 pins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
  Neopixel Strip -- White (30/m): These NeoPixel strips have 30 digitally-addressable pixel LEDs per meter and are very affordable and are only 12.5 mm wide, 10 mm if you remove the strip from the casing.
  Lithium Ion Polymer Battery 3.7v 1200mAh: Lithium ion polymer (also known as 'lipo' or 'lipoly') batteries are thin, light and powerful. The output ranges from 4.2V when completely charged to 3.7V. This battery has a capacity of 1200mAh for a total of about 4.5 Wh. The batteries come pre-attached with a genuine 2-pin JST-PH connector as shown and include the necessary protection circuitry.
  TP4056 Module: TP4056 Lithium Battery Charge Management Module Links: TP4056 website
  White Light Strip: he NeoPixel is 'split', one half is the RGB you know and love, the other half is a white LED with a yellow phosphor. Unlit, it resembles an egg yolk. Lit up these are insanely bright (like ow my eye hurts) and can be controlled with 8-bit PWM per channel (8 x 4 channels = 32-bit color overall). Great for adding lots of colorful + white dots to your project! NeoPixel LEDs use 800 KHz protocol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
  Header 6: Header 6 Standard 6-pin 0.1 header. Use with straight break away headers (SKU : PRT-00116), right angle break away headers (PRT-00553), swiss pins (PRT-00743), machine pins (PRT-00117), and female headers (PRT-00115). Molex polarized connector foot print use with SKU : PRT-08094 with associated crimp pins and housings. NOTES ON THE VARIANTS LOCK and LOCK_LONGPADS... This footprint was designed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
  mini boost module: mini boost module.
  Generic male header - 4 pins: Generic male header
